# Fritzing sketch UpdatedNEW_8to56charlie (saved by Fritzing 0.9.3b)
breadboards: 2

parts:
  LED1 = smd LED [color="Red (633nm)" package="1206 [SMD]"]
  LED2 = smd LED [color="Green (555nm)" package="1206 [SMD]"]
  R1 = Resistor [tolerance=±5% resistance=220 package="1206 [SMD]"]
  LED3 = smd LED [color="Green (555nm)" package="1206 [SMD]"]
  LED4 = smd LED [color="Green (555nm)" package="1206 [SMD]"]
  LED5 = smd LED [color="Green (555nm)" package="1206 [SMD]"]
  LED6 = smd LED [color="Red (633nm)" package="1206 [SMD]"]
  LED7 = smd LED [color="Green (555nm)" package="1206 [SMD]"]
  LED8 = smd LED [color="Green (555nm)" package="1206 [SMD]"]
  LED9 = smd LED [color="Green (555nm)" package="1206 [SMD]"]
  LED10 = smd LED [color="Green (555nm)" package="1206 [SMD]"]
  LED11 = smd LED [color="Red (633nm)" package="1206 [SMD]"]
  LED12 = smd LED [color="Orange (605nm)" package="1206 [SMD]"]
  LED13 = smd LED [color="Orange (605nm)" package="1206 [SMD]"]
  LED14 = smd LED [color="Orange (605nm)" package="1206 [SMD]"]
  R2 = Resistor [tolerance=±5% resistance=220 package="1206 [SMD]"]
  R3 = Resistor [tolerance=±5% resistance=220 package="1206 [SMD]"]
  R5 = Resistor [tolerance=±5% resistance=220 package="1206 [SMD]"]
  R6 = Resistor [tolerance=±5% resistance=220 package="1206 [SMD]"]
  R7 = Resistor [tolerance=±5% resistance=220 package="1206 [SMD]"]
  R8 = Resistor [tolerance=±5% resistance=220 package="1206 [SMD]"]
  R4 = Resistor [tolerance=±5% resistance=220 package="1206 [SMD]"]
  Part1 = Arduino Uno (Rev3) - ICSP
  7_Segment3 = 7 Segment Display
  7_Segment4 = 7 Segment Display
  S1 = Pushbutton [package="[THT]"]
  S2 = Pushbutton [package="[THT]"]
  R9 = Resistor [tolerance=±5% resistance=10k package=THT]
  R10 = Resistor [tolerance=±5% resistance=10k package=THT]
  C1 = Ceramic Capacitor [capacitance=4.7nF package="100 mil [THT, multilayer]"]
  C2 = Ceramic Capacitor [capacitance=4.7nF package="100 mil [THT, multilayer]"]

nets:
  N1: LED1.cathode, R2.Pin_1, 7_Segment3.Segment_B, 7_Segment4.Segment_B
  N2: LED1.anode, LED2.anode, R1.Pin_0, LED3.anode, LED4.anode, LED5.anode, LED6.anode, LED7.anode, Part1.D0/RX
  N3: LED2.cathode, LED9.cathode, R3.Pin_1, 7_Segment3.Segment_C
  N4: R1.Pin_1, LED8.cathode, 7_Segment3.Segment_A, 7_Segment4.Segment_A
  N5: LED3.cathode, LED10.cathode, R4.Pin_1, 7_Segment4.Segment_C
  N6: LED4.cathode, LED11.cathode, R5.Pin_1, 7_Segment3.Segment_D, 7_Segment4.Segment_D
  N7: LED5.cathode, LED12.cathode, R6.Pin_1, 7_Segment3.Segment_E, 7_Segment4.Segment_E
  N8: LED6.cathode, LED13.cathode, R7.Pin_1, 7_Segment3.Segment_F, 7_Segment4.Segment_F
  N9: LED7.cathode, LED14.cathode, R8.Pin_1, 7_Segment3.Segment_G, 7_Segment4.Segment_G
  N10: LED8.anode, LED9.anode, LED10.anode, LED11.anode, LED12.anode, LED13.anode, LED14.anode, R2.Pin_0, Part1.D1/TX
  N11: R3.Pin_0, Part1.D2, 7_Segment4.common_anode
  N12: R5.Pin_0, Part1.D4
  N13: R6.Pin_0, Part1.D5_PWM
  N14: R7.Pin_0, Part1.D6_PWM
  N15: R8.Pin_0, Part1.D7
  N16: R4.Pin_0, Part1.D3_PWM, 7_Segment3.common_anode
  N17: Part1.D8, S1.Pin_1, S1.Pin_2, R10.Pin_1, C1.1
  N18: Part1.D9_PWM, S2.Pin_1, S2.Pin_2, R9.Pin_1, C2.1
  N19: Part1.5V, R9.Pin_0, R10.Pin_0
  N20: Part1.GND, S1.Pin_3, S1.Pin_4, S2.Pin_3, S2.Pin_4, C1.0, C2.0
