# Fritzing sketch charlie (saved by Fritzing 0.9.3b)
breadboards: 1

parts:
  LED1 = LED - 3mm [color="Red (633nm)" package="3 mm [THT]"]
  LED2 = LED - 3mm [color="Red (633nm)" package="3 mm [THT]"]
  LED3 = LED - 3mm [color="Red (633nm)" package="3 mm [THT]"]
  LED4 = LED - 3mm [color="Red (633nm)" package="3 mm [THT]"]
  LED5 = LED - 3mm [color="Red (633nm)" package="3 mm [THT]"]
  LED6 = LED - 3mm [color="Red (633nm)" package="3 mm [THT]"]
  LED7 = LED - 3mm [color="Red (633nm)" package="3 mm [THT]"]
  LED8 = LED - 3mm [color="Red (633nm)" package="3 mm [THT]"]
  LED9 = LED - 3mm [color="Red (633nm)" package="3 mm [THT]"]
  LED10 = LED - 3mm [color="Red (633nm)" package="3 mm [THT]"]
  LED11 = LED - 3mm [color="Red (633nm)" package="3 mm [THT]"]
  LED12 = LED - 3mm [color="Red (633nm)" package="3 mm [THT]"]
  LED13 = LED - 3mm [color="Red (633nm)" package="3 mm [THT]"]
  LED14 = LED - 3mm [color="Red (633nm)" package="3 mm [THT]"]
  LED15 = LED - 3mm [color="Red (633nm)" package="3 mm [THT]"]
  LED16 = LED - 3mm [color="Red (633nm)" package="3 mm [THT]"]
  LED17 = LED - 3mm [color="Red (633nm)" package="3 mm [THT]"]
  LED18 = LED - 3mm [color="Red (633nm)" package="3 mm [THT]"]
  LED19 = LED - 3mm [color="Red (633nm)" package="3 mm [THT]"]
  LED20 = LED - 3mm [color="Red (633nm)" package="3 mm [THT]"]
  R1 = Resistor [tolerance=±5% resistance=220 package="0402 [SMD]"]
  R2 = Resistor [tolerance=±5% resistance=220 package="0402 [SMD]"]
  R3 = Resistor [tolerance=±5% resistance=220 package="0402 [SMD]"]
  R4 = Resistor [tolerance=±5% resistance=220 package="0402 [SMD]"]
  R5 = Resistor [tolerance=±5% resistance=220 package="0402 [SMD]"]
  Part1 = Arduino Uno (Rev3) - ICSP

nets (from the schematic view):
  N1: LED1.cathode, LED2.cathode, LED3.cathode, LED4.cathode, R1.Pin_1, Part1.D8
  N2: LED1.anode, LED10.anode, LED14.anode, LED18.anode, R2.Pin_0
  N3: LED2.anode, LED6.anode, LED15.anode, LED19.anode, R3.Pin_0
  N4: LED3.anode, LED7.anode, LED11.anode, LED20.anode, R4.Pin_0
  N5: LED4.anode, LED8.anode, LED12.anode, LED16.anode, R5.Pin_0
  N6: LED5.cathode, LED6.cathode, LED7.cathode, LED8.cathode, R2.Pin_1, Part1.D9_PWM
  N7: LED5.anode, LED9.anode, LED13.anode, LED17.anode, R1.Pin_0
  N8: LED9.cathode, LED10.cathode, LED11.cathode, LED12.cathode, R3.Pin_1, Part1.D10_PWM/SS
  N9: LED13.cathode, LED14.cathode, LED15.cathode, LED16.cathode, R4.Pin_1, Part1.D11_PWM/MOSI
  N10: LED17.cathode, LED18.cathode, LED19.cathode, LED20.cathode, R5.Pin_1, Part1.D12/MISO
