# Fritzing sketch charlie4to12 (saved by Fritzing 0.9.3b)
breadboards: 1

parts:
  Part1 = Arduino Uno (Rev3) - ICSP
  LED1 = LED - 5mm [color="Red (633nm)" package="5 mm [THT]"]
  LED2 = LED - 5mm [color="Green (555nm)" package="5 mm [THT]"]
  LED3 = LED - 5mm [color="Green (555nm)" package="5 mm [THT]"]
  LED4 = LED - 5mm [color="Green (555nm)" package="5 mm [THT]"]
  LED5 = LED - 5mm [color="Green (555nm)" package="5 mm [THT]"]
  LED6 = LED - 5mm [color="Red (633nm)" package="5 mm [THT]"]
  LED7 = LED - 5mm [color="Green (555nm)" package="5 mm [THT]"]
  LED8 = LED - 5mm [color="Green (555nm)" package="5 mm [THT]"]
  LED9 = LED - 5mm [color="Green (555nm)" package="5 mm [THT]"]
  LED10 = LED - 5mm [color="Green (555nm)" package="5 mm [THT]"]
  LED11 = LED - 5mm [color="Red (633nm)" package="5 mm [THT]"]
  LED12 = LED - 5mm [color="Blue (430nm)" package="5 mm [THT]"]
  R1 = Resistor [tolerance=±5% resistance=330 package="1206 [SMD]"]
  R2 = Resistor [tolerance=±5% resistance=330 package="1206 [SMD]"]
  R3 = Resistor [tolerance=±5% resistance=330 package="1206 [SMD]"]
  R4 = Resistor [tolerance=±5% resistance=330 package="1206 [SMD]"]

nets (from the schematic view):
  N1: Part1.D9_PWM, LED1.cathode, LED2.cathode, LED3.cathode, R1.Pin_1
  N2: Part1.D10_PWM/SS, LED4.cathode, LED5.cathode, LED6.cathode, R2.Pin_1
  N3: Part1.D11_PWM/MOSI, LED7.cathode, LED8.cathode, LED9.cathode, R3.Pin_1
  N4: Part1.D12/MISO, LED10.cathode, LED11.cathode, LED12.cathode, R4.Pin_1
  N5: LED1.anode, LED8.anode, LED11.anode, R2.Pin_0
  N6: LED2.anode, LED5.anode, LED12.anode, R3.Pin_0
  N7: LED3.anode, LED6.anode, LED9.anode, R4.Pin_0
  N8: LED4.anode, LED7.anode, LED10.anode, R1.Pin_0
