# Fritzing sketch charlie8to56comcat (saved by Fritzing 0.9.3b)
breadboards: 2

parts:
  LED1 = LED - 5mm [color="Red (633nm)" package="5 mm [THT]"]
  LED2 = LED - 5mm [color="Green (555nm)" package="5 mm [THT]"]
  LED3 = LED - 5mm [color="Green (555nm)" package="5 mm [THT]"]
  LED4 = LED - 5mm [color="Green (555nm)" package="5 mm [THT]"]
  LED5 = LED - 5mm [color="Green (555nm)" package="5 mm [THT]"]
  LED6 = LED - 5mm [color="Red (633nm)" package="5 mm [THT]"]
  LED7 = LED - 5mm [color="Green (555nm)" package="5 mm [THT]"]
  LED8 = LED - 5mm [color="Green (555nm)" package="5 mm [THT]"]
  LED9 = LED - 5mm [color="Green (555nm)" package="5 mm [THT]"]
  LED10 = LED - 5mm [color="Green (555nm)" package="5 mm [THT]"]
  LED11 = LED - 5mm [color="Red (633nm)" package="5 mm [THT]"]
  LED12 = LED - 5mm [color="Orange (605nm)" package="5 mm [THT]"]
  LED13 = LED - 5mm [color="Orange (605nm)" package="5 mm [THT]"]
  LED14 = LED - 5mm [color="Orange (605nm)" package="5 mm [THT]"]
  R1 = Resistor [tolerance=±5% resistance=220 package=THT]
  R2 = Resistor [tolerance=±5% resistance=220 package=THT]
  Part1 = Arduino Uno (Rev3) - ICSP
  7_Segment1 = 7 Segment Display
  7_Segment2 = 7 Segment Display
  R3 = Resistor [tolerance=±5% resistance=220 package=THT]
  R4 = Resistor [tolerance=±5% resistance=220 package=THT]
  R5 = Resistor [tolerance=±5% resistance=220 package=THT]
  R6 = Resistor [tolerance=±5% resistance=220 package=THT]
  R7 = Resistor [tolerance=±5% resistance=220 package=THT]
  R8 = Resistor [tolerance=±5% resistance=220 package=THT]

nets:
  N1: LED1.cathode, LED2.cathode, LED3.cathode, LED4.cathode, LED5.cathode, LED6.cathode, LED7.cathode, R1.Pin_0, Part1.D0/RX
  N2: LED1.anode, R2.Pin_1, 7_Segment1.Segment_F, 7_Segment2.Segment_F
  N3: LED2.anode, LED9.anode, 7_Segment2.Segment_E, R3.Pin_1
  N4: LED3.anode, LED10.anode, 7_Segment1.Segment_E, R4.Pin_1
  N5: LED4.anode, LED11.anode, 7_Segment1.Segment_D, 7_Segment2.Segment_D, R5.Pin_1
  N6: LED5.anode, LED12.anode, 7_Segment1.Segment_C, 7_Segment2.Segment_C, R6.Pin_1
  N7: LED6.anode, LED13.anode, 7_Segment1.Segment_B, 7_Segment2.Segment_B, R7.Pin_1
  N8: LED7.anode, LED14.anode, 7_Segment1.Segment_A, 7_Segment2.Segment_A, R8.Pin_1
  N9: LED8.cathode, LED9.cathode, LED10.cathode, LED11.cathode, LED12.cathode, LED13.cathode, LED14.cathode, R2.Pin_0, Part1.D1/TX
  N10: LED8.anode, R1.Pin_1, 7_Segment1.Segment_G, 7_Segment2.Segment_G
  N11: Part1.D2, R5.Pin_0
  N12: Part1.D3_PWM, R6.Pin_0
  N13: Part1.D4, R7.Pin_0
  N14: Part1.D5_PWM, R8.Pin_0
  N15: 7_Segment1.common_cathode, R3.Pin_0
  N16: 7_Segment2.common_cathode, R4.Pin_0
